# Fritzing sketch diagram (saved by Fritzing 0.9.3b)

parts:
  U1 = RFID RC522 SIP - 8 pins [chip_label="RFID RC522" package="SIP (Single Inline) [THT]"]
  Part1 = Arduino Uno (Rev3) - ICSP
  Part2 = Arduino Uno (Rev3) - ICSP
  RELAY = LED - 3mm [color="Red (633nm)" package="3 mm [THT]"]
  R1 = Resistor [tolerance=±5% resistance=1k package="0603 [SMD]"]
  DFPlayer_Mini1 = DFPlayer MINI [package="DIP (Dual Inline) [THT]"]
  SP1 = SPEAKER [package=pcb_mount_speaker]
  VCC1 = 4 x AAA Battery Mount

nets:
  N1: U1.NSS, Part1.D10_PWM/SS
  N2: U1.SCK, Part1.D13/SCK
  N3: U1.MOSI, Part1.D11_PWM/MOSI
  N4: U1.MISO, Part1.ICSP_MISO, Part1.D12/MISO
  GND: U1.GND, Part1.GND
  N5: U1.RST, Part1.D9_PWM
  VCC: U1.VCC, Part1.3V3
  N6: Part1.D0/RX, DFPlayer_Mini1.TX
  N7: Part1.D1/TX, R1.Pin_0
  N8: Part1.D5_PWM, Part2.D2
  N9: Part2.ICSP_MOSI, Part2.D11_PWM/MOSI, RELAY.anode
  N10: R1.Pin_1, DFPlayer_Mini1.RX
  N11: DFPlayer_Mini1.SPK1, SP1.-
  N12: DFPlayer_Mini1.GND, VCC1.-
  N13: DFPlayer_Mini1.SPK2, SP1.+

custom parts:
  RFID RC522 SIP - 8 pins: A SIP stand-in part for RFID RC522 . With 8 pins on a 300 mil single inline package (SIP) footprint.
  DFPlayer MINI: MP3 module by DFRobot.com for playing Music from an SD-Card. Supports WAV and MP3 files.
